// Logisim project 12-bit-risc-v-microprocessor.circ as structural Verilog: 2 circuits, main circuit main
module main (
);

  register_file_12_bit register_file_12_bit_1 ();  // open: Write_Enabler, Write_Data, RD_Selector, DATA_1_RS, RS_Selector, DATA_2_RT, RT_Selector, CLOCK, Register_Clear
endmodule

module register_file_12_bit (
  input  Write_Enabler,
  input  [11:0] Write_Data,
  input  [2:0] RS_Selector,
  input  [2:0] RD_Selector,
  input  [2:0] RT_Selector,
  input  CLOCK,
  input  Register_Clear,
  output [11:0] DATA_1_RS,
  output [11:0] DATA_2_RT
);

  wire and_1_out, and_2_out, and_3_out, and_4_out, and_5_out, and_6_out, and_7_out, and_8_out,
       decoder_1_out0, decoder_1_out1, decoder_1_out2, decoder_1_out3, decoder_1_out4, decoder_1_out5,
       decoder_1_out6, decoder_1_out7;
  wire [11:0] R0_q, R1_q, R2_q, R3_q, R4_q, R5_q, R6_q, R7_q;

  Decoder #(.select(3), .enable("false")) decoder_1 (
    .out0(decoder_1_out0), .out1(decoder_1_out1), .out2(decoder_1_out2), .out3(decoder_1_out3),
    .out4(decoder_1_out4), .out5(decoder_1_out5), .out6(decoder_1_out6), .out7(decoder_1_out7),
    .sel(RD_Selector));
  and and_1 (and_1_out, Write_Enabler, decoder_1_out0);
  and and_2 (and_2_out, Write_Enabler, decoder_1_out1);
  and and_3 (and_3_out, Write_Enabler, decoder_1_out2);
  and and_4 (and_4_out, Write_Enabler, decoder_1_out3);
  Register #(.width(12)) R0 (.D(Write_Data), .en(and_1_out), .Q(R0_q), .clk(CLOCK), .clr(Register_Clear));
  Register #(.width(12)) R1 (.D(Write_Data), .en(and_2_out), .Q(R1_q), .clk(CLOCK), .clr(Register_Clear));
  Register #(.width(12)) R2 (.D(Write_Data), .en(and_3_out), .Q(R2_q), .clk(CLOCK), .clr(Register_Clear));
  Register #(.width(12)) R3 (.D(Write_Data), .en(and_4_out), .Q(R3_q), .clk(CLOCK), .clr(Register_Clear));
  Register #(.width(12)) R7 (.D(Write_Data), .en(and_5_out), .Q(R7_q), .clk(CLOCK), .clr(Register_Clear));
  Register #(.width(12)) R6 (.D(Write_Data), .en(and_6_out), .Q(R6_q), .clk(CLOCK), .clr(Register_Clear));
  Register #(.width(12)) R5 (.D(Write_Data), .en(and_7_out), .Q(R5_q), .clk(CLOCK), .clr(Register_Clear));
  Register #(.width(12)) R4 (.D(Write_Data), .en(and_8_out), .Q(R4_q), .clk(CLOCK), .clr(Register_Clear));
  and and_5 (and_5_out, Write_Enabler, decoder_1_out7);
  and and_6 (and_6_out, Write_Enabler, decoder_1_out6);
  and and_7 (and_7_out, Write_Enabler, decoder_1_out5);
  and and_8 (and_8_out, Write_Enabler, decoder_1_out4);
  Multiplexer #(.select(3), .width(12), .enable("false")) multiplexer_1 (
    .in0(R0_q), .in1(R1_q), .in2(R2_q), .in3(R3_q), .in4(R4_q), .in5(R5_q), .in6(R6_q), .in7(R7_q),
    .out(DATA_1_RS), .sel(RS_Selector));
  Multiplexer #(.select(3), .width(12), .enable("false")) multiplexer_2 (
    .in0(R0_q), .in1(R1_q), .in2(R2_q), .in3(R3_q), .in4(R4_q), .in5(R5_q), .in6(R6_q), .in7(R7_q),
    .out(DATA_2_RT), .sel(RT_Selector));
endmodule
